# Fritzing sketch Smart Alarm (saved by Fritzing 1.0.4)
breadboards: 1

parts:
  J1 = STM32 Nucleo boards
  OLED_I2C1 = OLED 128x64 I2C Monochrome Display
  A1 = Wemos S2 Mini [part_number="WeMos D1 Mini Lite"]
  Keypad4x2 = Keypad Membran 4x4
  S1 = SWITCH-MOMENTARY-2 [package=reed_switch_pth]
  J2 = Piezo Speaker
  10K = Resistor [tolerance=±5% power=0.25W resistance=220 package=THT]

nets:
  N1: J1.PC6, Keypad4x2.Pin5
  N2: J1.PC5, Keypad4x2.Pin8
  N3: J1.D2, J2.pin2
  N4: J1.D4, A1.Pin_1, A1.Pin_9
  N5: J1.D7, S1.2, 10K.Pin_1
  3V3: J1.3V3, OLED_I2C1.VDD, 10K.Pin_0
  N6: J1.5V, A1.Pin_17, A1.Pin_25
  GND: J1.GND, OLED_I2C1.GND, A1.Pin_18, A1.Pin_26, S1.1, J2.pin1
  N7: J1.PB2, Keypad4x2.Pin3
  N8: J1.PB1, Keypad4x2.Pin2
  N9: J1.PC4, Keypad4x2.Pin7
  N10: J1.PC9, OLED_I2C1.SCK, A1.Pin_24, A1.Pin_32
  N11: J1.PB8, OLED_I2C1.SDA, A1.Pin_23, A1.Pin_31
  N12: J1.PC7, Keypad4x2.Pin6
  N13: J1.PB10, Keypad4x2.Pin4
  N14: J1.PB0, Keypad4x2.Pin1
  N15: A1.Pin_2, A1.Pin_10
  N16: A1.Pin_3, A1.Pin_11
  N17: A1.Pin_4, A1.Pin_12
  N18: A1.Pin_5, A1.Pin_13
  N19: A1.Pin_6, A1.Pin_14
  N20: A1.Pin_7, A1.Pin_15
  N21: A1.Pin_8, A1.Pin_16
  N22: A1.Pin_19, A1.Pin_27
  N23: A1.Pin_20, A1.Pin_28
  N24: A1.Pin_21, A1.Pin_29
  N25: A1.Pin_22, A1.Pin_30

custom parts:
  Wemos S2 Mini: A mini wifi board based on the ESP32-S2FN4R2.
  Keypad Membran 4x4: Membrane Keypad 4x4 Matrix
